# Fritzing sketch mainBoard (saved by Fritzing 0.9.3b)
perfboards: 1

parts:
  arduino_mega_pro_mini1 = arduino mega pro mini [chip_label="arduino mega pro mini" package="DIP (Dual Inline) [THT]"]
  POWER = male pin header, 4 pins [form="♂ (male)"]
  A10 = male pin header, 4 pins [form="♂ (male)"]
  A8 = male pin header, 4 pins [form="♂ (male)"]
  A6 = male pin header, 4 pins [form="♂ (male)"]
  J3 = male pin header, 4 pins [form="♂ (male)"]
  A2 = male pin header, 4 pins [form="♂ (male)"]
  POWER_2 = male pin header, 4 pins [form="♂ (male)"]
  POWER_3 = male pin header, 4 pins [form="♂ (male)"]
  POWER_4 = male pin header, 4 pins [form="♂ (male)"]
  POWER_5 = male pin header, 4 pins [form="♂ (male)"]
  POWER_6 = male pin header, 4 pins [form="♂ (male)"]
  POWER_7 = male pin header, 4 pins [form="♂ (male)"]
  POWER_8 = male pin header, 4 pins [form="♂ (male)"]
  POWER_9 = male pin header, 4 pins [form="♂ (male)"]
  POWER_10 = male pin header, 4 pins [form="♂ (male)"]
  D7 = male pin header, 2 pins [form="♂ (male)"]
  D9 = male pin header, 2 pins [form="♂ (male)"]
  D13 = male pin header, 2 pins [form="♂ (male)"]
  J24 = male pin header, 2 pins [form="♂ (male)"]
  J25 = male pin header, 2 pins [form="♂ (male)"]
  D6 = male pin header, 2 pins [form="♂ (male)"]
  D8 = male pin header, 2 pins [form="♂ (male)"]
  D12 = male pin header, 2 pins [form="♂ (male)"]
  Serial3 = male pin header, 4 pins [form="♂ (male)"]
  Serial2 = male pin header, 4 pins [form="♂ (male)"]
  I2C = male pin header, 4 pins [form="♂ (male)"]
  SPI(D50_D51_D52_5V_SPI_GND_SPI_) = male pin header, 6 pins [form="♂ (male)"]
  Servo2(A12_A14_D44_D46D48_D47) = male pin header, 6 pins [form="♂ (male)"]
  Servo3(D37_D39_D41_D43_D45_D49) = male pin header, 6 pins [form="♂ (male)"]
  Servo4(A9_A11_A13_A15_D33_D35) = male pin header, 6 pins [form="♂ (male)"]
  Servo0(D26_D28_D30_D31_D29_D27) = male pin header, 6 pins [form="♂ (male)"]
  D10 = male pin header, 2 pins [form="♂ (male)"]
  D11 = male pin header, 2 pins [form="♂ (male)"]
  A1 = male pin header, 4 pins [form="♂ (male)"]
  A3 = male pin header, 4 pins [form="♂ (male)"]
  A5 = male pin header, 4 pins [form="♂ (male)"]
  A7 = male pin header, 4 pins [form="♂ (male)"]
  BATTERY = female pin header, 2 pins [form="♀ (female)"]
  Servo1(D32_D34_D36_D38_D40_D42) = male pin header, 6 pins [form="♂ (male)"]
  MODE(D24) = male pin header, 2 pins [form="♂ (male)"]
  R1 = Resistor [tolerance=±5% resistance=1k package=THT]
  LED1 = LED - 3mm [color="White (4500K)" package="3 mm [THT]"]

nets:
  5V: arduino_mega_pro_mini1.VIN1, POWER.pin1, POWER.pin4, POWER_2.pin1, POWER_2.pin4, POWER_3.pin1, POWER_3.pin4, POWER_4.pin1, POWER_4.pin4, POWER_5.pin1, POWER_5.pin4, POWER_6.pin1, POWER_6.pin4, POWER_7.pin1, POWER_7.pin4, POWER_8.pin1, POWER_8.pin4, POWER_9.pin1, POWER_9.pin4, POWER_10.pin1, POWER_10.pin4, BATTERY.pin1
  N1: arduino_mega_pro_mini1.GND0, A10.pin3, A8.pin3, A6.pin3, J3.pin3, A2.pin3, A1.pin2, A3.pin2, A5.pin2, A7.pin2, MODE(D24).pin1, LED1.cathode
  GND: arduino_mega_pro_mini1.GND1, POWER.pin2, POWER.pin3, POWER_2.pin2, POWER_2.pin3, POWER_3.pin2, POWER_3.pin3, POWER_4.pin2, POWER_4.pin3, POWER_5.pin2, POWER_5.pin3, POWER_6.pin2, POWER_6.pin3, POWER_7.pin2, POWER_7.pin3, POWER_8.pin2, POWER_8.pin3, POWER_9.pin2, POWER_9.pin3, POWER_10.pin2, POWER_10.pin3, D7.pin1, D9.pin1, D13.pin1, J24.pin1, J25.pin1, D6.pin1, D8.pin1, D12.pin1, Serial3.pin2, Serial2.pin2, I2C.pin3, D10.pin1, D11.pin1, BATTERY.pin2
  N2: arduino_mega_pro_mini1.5V0, A10.pin2, A8.pin2, A6.pin2, J3.pin2, A2.pin2, A1.pin3, A3.pin3, A5.pin3, A7.pin3
  N3: arduino_mega_pro_mini1.5V1, Serial3.pin1, Serial2.pin1, I2C.pin4
  N4: arduino_mega_pro_mini1.3V3_0, A10.pin1, A8.pin1, A6.pin1, J3.pin1, A2.pin1, A1.pin4, A3.pin4, A5.pin4, A7.pin4
  N5: arduino_mega_pro_mini1.D4, J25.pin2
  N6: arduino_mega_pro_mini1.D5, J24.pin2
  N7: arduino_mega_pro_mini1.D6, D6.pin2
  N8: arduino_mega_pro_mini1.D7, D7.pin2
  N9: arduino_mega_pro_mini1.D8, D8.pin2
  N10: arduino_mega_pro_mini1.D9, D9.pin2
  N11: arduino_mega_pro_mini1.D10, D10.pin2
  N12: arduino_mega_pro_mini1.D11, D11.pin2
  N13: arduino_mega_pro_mini1.D12, D12.pin2
  N14: arduino_mega_pro_mini1.D13, D13.pin2
  N15: arduino_mega_pro_mini1.D14, Serial3.pin3
  N16: arduino_mega_pro_mini1.D15, Serial3.pin4
  N17: arduino_mega_pro_mini1.D16, Serial2.pin3
  N18: arduino_mega_pro_mini1.D17, Serial2.pin4
  N19: arduino_mega_pro_mini1.D20, I2C.pin1
  N20: arduino_mega_pro_mini1.D21, I2C.pin2
  N21: arduino_mega_pro_mini1.D22, R1.Pin_0
  N22: arduino_mega_pro_mini1.D24, MODE(D24).pin2
  N23: arduino_mega_pro_mini1.D26, Servo0(D26_D28_D30_D31_D29_D27).pin1
  N24: arduino_mega_pro_mini1.D27, Servo0(D26_D28_D30_D31_D29_D27).pin6
  N25: arduino_mega_pro_mini1.D28, Servo0(D26_D28_D30_D31_D29_D27).pin2
  N26: arduino_mega_pro_mini1.D29, Servo0(D26_D28_D30_D31_D29_D27).pin5
  N27: arduino_mega_pro_mini1.D30, Servo0(D26_D28_D30_D31_D29_D27).pin3
  N28: arduino_mega_pro_mini1.D31, Servo0(D26_D28_D30_D31_D29_D27).pin4
  N29: arduino_mega_pro_mini1.D32, Servo1(D32_D34_D36_D38_D40_D42).pin6
  N30: arduino_mega_pro_mini1.D33, Servo4(A9_A11_A13_A15_D33_D35).pin2
  N31: arduino_mega_pro_mini1.D34, Servo1(D32_D34_D36_D38_D40_D42).pin5
  N32: arduino_mega_pro_mini1.D35, Servo4(A9_A11_A13_A15_D33_D35).pin1
  N33: arduino_mega_pro_mini1.D36, Servo1(D32_D34_D36_D38_D40_D42).pin4
  N34: arduino_mega_pro_mini1.D37, Servo3(D37_D39_D41_D43_D45_D49).pin6
  N35: arduino_mega_pro_mini1.D38, Servo1(D32_D34_D36_D38_D40_D42).pin3
  N36: arduino_mega_pro_mini1.D39, Servo3(D37_D39_D41_D43_D45_D49).pin5
  N37: arduino_mega_pro_mini1.D40, Servo1(D32_D34_D36_D38_D40_D42).pin2
  N38: arduino_mega_pro_mini1.D41, Servo3(D37_D39_D41_D43_D45_D49).pin4
  N39: arduino_mega_pro_mini1.D42, Servo1(D32_D34_D36_D38_D40_D42).pin1
  N40: arduino_mega_pro_mini1.D43, Servo3(D37_D39_D41_D43_D45_D49).pin3
  N41: arduino_mega_pro_mini1.D44, Servo2(A12_A14_D44_D46D48_D47).pin4
  N42: arduino_mega_pro_mini1.D45, Servo3(D37_D39_D41_D43_D45_D49).pin2
  N43: arduino_mega_pro_mini1.D46, Servo2(A12_A14_D44_D46D48_D47).pin3
  N44: arduino_mega_pro_mini1.D47, Servo2(A12_A14_D44_D46D48_D47).pin1
  N45: arduino_mega_pro_mini1.D48, Servo2(A12_A14_D44_D46D48_D47).pin2
  N46: arduino_mega_pro_mini1.D49, Servo3(D37_D39_D41_D43_D45_D49).pin1
  N47: arduino_mega_pro_mini1.D50, SPI(D50_D51_D52_5V_SPI_GND_SPI_).pin6
  N48: arduino_mega_pro_mini1.D51, SPI(D50_D51_D52_5V_SPI_GND_SPI_).pin5
  N49: arduino_mega_pro_mini1.D52, SPI(D50_D51_D52_5V_SPI_GND_SPI_).pin4
  N50: arduino_mega_pro_mini1.D53, SPI(D50_D51_D52_5V_SPI_GND_SPI_).pin3
  N51: arduino_mega_pro_mini1.A1, A1.pin1
  N52: arduino_mega_pro_mini1.A2, A2.pin4
  N53: arduino_mega_pro_mini1.A3, A3.pin1
  N54: arduino_mega_pro_mini1.A4, J3.pin4
  N55: arduino_mega_pro_mini1.A5, A5.pin1
  N56: arduino_mega_pro_mini1.A6, A6.pin4
  N57: arduino_mega_pro_mini1.A7, A7.pin1
  N58: arduino_mega_pro_mini1.A8, A8.pin4
  N59: arduino_mega_pro_mini1.A9, Servo4(A9_A11_A13_A15_D33_D35).pin6
  N60: arduino_mega_pro_mini1.A10, A10.pin4
  N61: arduino_mega_pro_mini1.A11, Servo4(A9_A11_A13_A15_D33_D35).pin5
  N62: arduino_mega_pro_mini1.A12, Servo2(A12_A14_D44_D46D48_D47).pin6
  N63: arduino_mega_pro_mini1.A13, Servo4(A9_A11_A13_A15_D33_D35).pin4
  N64: arduino_mega_pro_mini1.A14, Servo2(A12_A14_D44_D46D48_D47).pin5
  N65: arduino_mega_pro_mini1.A15, Servo4(A9_A11_A13_A15_D33_D35).pin3
  N66: arduino_mega_pro_mini1.ICSP_GND, SPI(D50_D51_D52_5V_SPI_GND_SPI_).pin1
  N67: arduino_mega_pro_mini1.ICSP_5V, SPI(D50_D51_D52_5V_SPI_GND_SPI_).pin2
  N68: R1.Pin_1, LED1.anode

custom parts:
  arduino mega pro mini: It's an arduino mega pro mini patrs
